// Logisim project Principal _Projeto_completo.circ as structural Verilog: 1 circuit, main circuit main
// Display
module main (
  input  in_1,
  input  in_2,
  input  in_3,
  input  in_4,
  input  in_5,
  input  in_6,
  input  in_7,
  input  in_8
);

  wire Comparador_p9, LED_RGB_p9, LED_RGB_p10;
  wire [3:0] \Circuito_completo_diferença_out_10 ;

  \Diferença_main  \Circuito_completo_diferença  (
    .Alet_4(in_1), .Alet_3(in_2), .Alet_2(in_3), .Alet_1(in_4), .\Bit_de_seleção (Comparador_p9),
    .Bit_4(in_5), .Bit3(in_6), .Bit2(in_7), .Bit1(in_8), .out_10(\Circuito_completo_diferença_out_10 ));
  LED led_1 (.in(Comparador_p9));
  // comparador Comparador: pin names not known; wires that end beside it: in_1, in_5, in_2, in_6, in_3, in_7, in_4, in_8, Comparador_p9
  // Divisor LED_RGB: pin names not known; wires that end beside it: \Circuito_completo_diferença_out_10 [3], \Circuito_completo_diferença_out_10 [2], \Circuito_completo_diferença_out_10 [1], \Circuito_completo_diferença_out_10 [0], \Circuito_completo_diferença_out_10 [1], \Circuito_completo_diferença_out_10 [0], \Circuito_completo_diferença_out_10 [1], \Circuito_completo_diferença_out_10 [0], LED_RGB_p9, LED_RGB_p10, \Circuito_completo_diferença_out_10 [3], \Circuito_completo_diferença_out_10 [2], \Circuito_completo_diferença_out_10 [1], \Circuito_completo_diferença_out_10 [0]
  // circuito Display: pin names not known; wires that end beside it: in_5, in_6, in_7, in_8
  // RGBLed #(.multibit("true")) LED_2: pin names not known; wires that end beside it: LED_RGB_p9, LED_RGB_p10
endmodule
